# Fritzing sketch vehicle-simulator (saved by Fritzing 0.9.2b)
breadboards: 1

parts:
  LED2 = LED - 5mm [color="Yellow (585nm)" package="5 mm [THT]"]
  LED3 = LED - 5mm [color="Yellow (585nm)" package="5 mm [THT]"]
  S1 = Pushbutton [package="[THT]"]
  LED9 = LED - 5mm [color="Green (560nm)" package="5 mm [THT]"]
  Part1 = Intel Edison Arduinobreakout
  LED10 = LED - 5mm [color="White (6500K)" package="5 mm [THT]"]
  LED11 = LED - 5mm [color="White (6500K)" package="5 mm [THT]"]
  R1 = Resistor [tolerance=±5% resistance=33 package=THT]
  R2 = Resistor [tolerance=±5% resistance=33 package=THT]
  R3 = Resistor [tolerance=±5% resistance=33 package=THT]
  LED12 = LED - 5mm [color="Red (635nm)" package="5 mm [THT]"]
  LED13 = LED - 5mm [color="Red (635nm)" package="5 mm [THT]"]
  R4 = Resistor [tolerance=±5% resistance=33 package=THT]
  R5 = Resistor [tolerance=±5% resistance=33 package=THT]
  R6 = Resistor [tolerance=±5% resistance=33 package=THT]
  R7 = Resistor [tolerance=±5% resistance=33 package=THT]
  LED14 = LED - 5mm [color="Red (635nm)" package="5 mm [THT]"]
  LED15 = LED - 5mm [color="Red (635nm)" package="5 mm [THT]"]
  R8 = Resistor [tolerance=±5% resistance=33 package=THT]
  R9 = Resistor [tolerance=±5% resistance=33 package=THT]
  J1 = Piezo Speaker
  J2 = Basic Servo

nets:
  N1: LED2.cathode, R6.Pin_1
  N2: LED2.anode, LED3.anode, Part1.D2
  N3: LED3.cathode, R9.Pin_1
  N4: S1.Pin_1, S1.Pin_2, Part1.D7
  N5: S1.Pin_3, S1.Pin_4, LED9.anode
  N6: LED9.cathode, R3.Pin_1
  N7: Part1.D8, LED15.anode
  N8: Part1.D9_PWM, LED13.anode
  N9: Part1.D10_PWM/SS, LED12.anode
  N10: Part1.D11_PWM/MOSI, LED14.anode
  N11: Part1.D12/MISO, J1.pin2
  N12: Part1.D13/SCK, LED10.anode, LED11.anode
  GND: Part1.GND, R1.Pin_0, R2.Pin_0, R3.Pin_0, R4.Pin_0, R5.Pin_0, R6.Pin_0, R7.Pin_0, R8.Pin_0, R9.Pin_0, J1.pin1, J2.gnd
  N13: Part1.D3_PWM, J2.pulse
  3V3: Part1.3V3, J2.vcc
  N14: LED10.cathode, R2.Pin_1
  N15: LED11.cathode, R1.Pin_1
  N16: LED12.cathode, R4.Pin_1
  N17: LED13.cathode, R5.Pin_1
  N18: R7.Pin_1, LED14.cathode
  N19: LED15.cathode, R8.Pin_1
